# Fritzing sketch design (saved by Fritzing 0.9.3b)
breadboards: 1

parts:
  Linh_kiện1 = Arduino Uno (Rev3)
  hc-sr1 = hc-sr04
  J1 = Basic Servo

nets:
  N1: Linh_kiện1.D8, hc-sr1.Trig
  N2: Linh_kiện1.D3_PWM, J1.pulse
  N3: Linh_kiện1.D7, hc-sr1.Echo
  VCC: Linh_kiện1.5V, hc-sr1.VCC, J1.vcc
  GND: Linh_kiện1.GND, hc-sr1.GND, J1.gnd
